# Fritzing sketch Sketch_Jewel_2 (saved by Fritzing 0.9.0b)

parts:
  Arduino1 = Arduino Mini (Rev5)
  Composant1 = LilyPad LED
  Composant2 = LilyPad LED
  Composant3 = LilyPad LED
  Composant4 = LilyPad LED
  Composant5 = LilyPad LED
  Composant6 = LilyPad LED
  Composant7 = LilyPad LED
  S1 = Round Pushbutton
  R1 = PHOTOCELL [package=photocell]
  R2 = Resistor [tolerance=±5% resistance=10k package="0603 [SMD]"]

nets:
  N1: Arduino1.GND, Composant4.-, Composant5.-, Composant6.-, Composant7.-, S1.leg0
  N2: Arduino1.D5_PWM, Composant6.+
  N3: Arduino1.D6_PWM, Composant5.+
  N4: Arduino1.D7, Composant7.+
  N5: Arduino1.D8, Composant4.+
  N6: Arduino1.VCC, Composant1.-, Composant2.-, Composant3.-
  N7: Arduino1.5V, R1.P$2
  N8: Arduino1.A3, R1.P$1, R2.Pin_1
  N9: Arduino1.D13, Composant1.+
  N10: Arduino1.D12, Composant2.+
  N11: Arduino1.D11_PWM, Composant3.+

notes:
  Batterie
  5V GRND
